# Fritzing sketch lm35_term (saved by Fritzing 0.9.3b)
breadboards: 1

parts:
  Eleman1 = Arduino Uno (Rev3)
  T1 = LM35 Temperature Sensor [package="TO92 [THT]"]
  U1 = LCD-16X2 [package=lcd-16x2_noholes]
  U2 = POT [package=pot_mammoth]

nets:
  N1: Eleman1.A0, T1.Vout
  N2: Eleman1.D11_PWM/MOSI, U1.E
  N3: Eleman1.D12/MISO, U1.RS
  N4: Eleman1.D2, U1.DB7
  N5: Eleman1.D3_PWM, U1.DB6
  N6: Eleman1.D4, U1.DB5
  N7: Eleman1.D5_PWM, U1.DB4
  5V: Eleman1.5V, T1.+Vs, U1.VDD, U1.A
  GND: Eleman1.GND, T1.GND, U1.VSS
  N8: U1.VO, U2.A
